# Fritzing sketch PLC 0-10V interface (saved by Fritzing 0.9.1b)

parts:
  proto5 = Adafruit_PermaProto_1_4_Board
  J7 = Screw terminal - 2 pins [package=THT]  # not connected
  U6 = mystery part, 8 pins [chip_label=LM2904]  # not connected
  R4 = Resistor [tolerance=±5% resistance=22k package="1206 [SMD]"]  # not connected
  C5 = Electrolytic Capacitor [capacitance=22µF package="100 mil [THT, electrolytic]"]  # not connected
  J10 = Screw terminal - 2 pins [package=THT]  # not connected
  C6 = Electrolytic Capacitor [capacitance=2.2µF package="100 mil [THT, electrolytic]"]  # not connected
  C7 = Electrolytic Capacitor [capacitance=2.2µF package="100 mil [THT, electrolytic]"]  # not connected
  R6 = Resistor [tolerance=±5% resistance=100k package=THT]  # not connected
  R7 = Resistor [tolerance=±5% resistance=100k package=THT]  # not connected
  R8 = Resistor [tolerance=±5% resistance=100k package=THT]  # not connected
  R9 = Resistor [tolerance=±5% resistance=100k package=THT]  # not connected
  J8 = screw terminal, 2 pins  # not connected
  J11 = screw terminal, 2 pins  # not connected
  J12 = screw terminal, 2 pins  # not connected
  U7 = mystery part, 3 pins [chip_label=TSR12450]  # not connected
  R5 = Resistor [tolerance=±5% resistance=22k package="1206 [SMD]"]  # not connected

nets:
  N1: proto5.connectorA1, proto5.connectorX1
  N2: proto5.connectorA7, proto5.connectorX7
  N3: proto5.connectorD4, proto5.connectorE2
  N4: proto5.connectorE10, proto5.connectorF10
  N5: proto5.connectorF13, proto5.connectorX13
  N6: proto5.connectorF14, proto5.connectorW14
  N7: proto5.connectorG5, proto5.connectorI2
  N8: proto5.connectorJ1, proto5.connectorZ1
  N9: proto5.connectorJ4, proto5.connectorY4
  N10: proto5.connectorJ12, proto5.connectorY12
  N11: proto5.connectorJ13, proto5.connectorZ13

notes:
  24VDC
  5VDC
  0-10V PLC OUT2
  0-10V PLC OUT1
  PWM IN1,2
  Arduino PLC 0-10V Interface
  Convert PLC 24VDC to 5VDC to power Arduino
  Convert the PWM output to analog with an RC network then use an OP AMP configured as a voltage doubler with the rails at 24V for a standard PLC 0-10V AI input
